# Fritzing sketch Vasukumar_Patel_Lab2 (saved by Fritzing 1.0.1rc)
breadboards: 1

parts:
  Part1 = Arduino Mega 2560 (Rev3)
  LED1 = smd LED [color="Red (633nm)" package="0603 [SMD]"]
  LED2 = smd LED [color="Yellow (595nm)" package="0603 [SMD]"]
  LED3 = smd LED [color="Green (570nm)" package="0603 [SMD]"]
  LED4 = smd LED [color="Red (633nm)" package="0603 [SMD]"]
  LED5 = smd LED [color="Green (570nm)" package="0603 [SMD]"]
  S1 = Momentary Switch [package=ksa_sealed_tac_switch]
  R1 = Resistor [tolerance=±5% power=0.25W resistance=220 package=THT]
  R2 = Resistor [tolerance=±5% power=0.25W resistance=220 package=THT]
  R3 = Resistor [tolerance=±5% power=0.25W resistance=220 package=THT]
  R4 = Resistor [tolerance=±5% power=0.25W resistance=220 package=THT]
  R5 = Resistor [tolerance=±5% power=0.25W resistance=220 package=THT]
  R6 = Resistor [tolerance=±5% power=0.25W resistance=220 package=THT]

nets:
  N1: Part1.D12_PWM, R6.Pin_0
  N2: Part1.D11_PWM, R5.Pin_0
  N3: Part1.D10_PWM, R3.Pin_0
  N4: Part1.D9_PWM, R2.Pin_0
  N5: Part1.D8_PWM, R1.Pin_0
  N6: Part1.GND, LED1.cathode, LED2.cathode, LED3.cathode, LED4.cathode, LED5.cathode, R4.Pin_0
  N7: Part1.D2_PWM, S1.1
  N8: LED1.anode, R1.Pin_1
  N9: LED2.anode, R2.Pin_1
  N10: LED3.anode, R3.Pin_1
  N11: LED4.anode, R5.Pin_1
  N12: LED5.anode, R6.Pin_1
  N13: S1.2, R4.Pin_1
