# Fritzing sketch Vasukumar_Patel_Lab4 (saved by Fritzing 1.0.1rc)
breadboards: 1

parts:
  Part1 = Arduino Mega 2560 (Rev3)
  S2 = Pushbutton [package="[THT]"]
  S3 = Pushbutton [package="[THT]"]
  S4 = Pushbutton [package="[THT]"]
  LED1 = smd LED [color="Yellow (595nm)" package="0603 [SMD]"]
  R1 = Resistor [tolerance=±5% power=0.25W resistance=220 package=THT]
  LED2 = smd LED [color="Red (633nm)" package="0603 [SMD]"]
  LED3 = smd LED [color="Green (570nm)" package="0603 [SMD]"]
  LED4 = smd LED [color="Blue (525nm)" package="0603 [SMD]"]
  LED5 = RGB LED (com. anode, rbg) [color="Red (633nm)" current=0.030A package="5 mm [THT]"]
  R2 = Resistor [tolerance=±5% power=0.25W resistance=220 package=THT]
  R3 = Resistor [tolerance=±5% power=0.25W resistance=220 package=THT]
  R4 = Resistor [tolerance=±5% power=0.25W resistance=220 package=THT]
  R5 = Resistor [tolerance=±5% power=0.25W resistance=220 package=THT]
  R6 = Resistor [tolerance=±5% power=0.25W resistance=220 package=THT]
  R7 = Resistor [tolerance=±5% power=0.25W resistance=220 package=THT]

nets:
  N1: Part1.D21/SCL, S2.Pin_1, S2.Pin_2
  N2: Part1.D20/SDA, S3.Pin_1, S3.Pin_2
  N3: Part1.D19/RX1, S4.Pin_1, S4.Pin_2
  N4: Part1.D13_PWM, R7.Pin_1
  N5: Part1.D12_PWM, R6.Pin_1
  N6: Part1.D11_PWM, R5.Pin_1
  N7: Part1.GND, S2.Pin_3, S2.Pin_4, S3.Pin_3, S3.Pin_4, S4.Pin_3, S4.Pin_4, LED1.cathode, LED2.cathode, LED3.cathode, LED4.cathode, LED5.common_anode
  N8: Part1.D1_TX0, R1.Pin_1
  N9: Part1.D5_PWM, R2.Pin_1
  N10: Part1.D6_PWM, R3.Pin_1
  N11: Part1.D7_PWM, R4.Pin_1
  N12: LED1.anode, R1.Pin_0
  N13: LED2.anode, R2.Pin_0
  N14: LED3.anode, R3.Pin_0
  N15: LED4.anode, R4.Pin_0
  N16: LED5.red_cathode, R7.Pin_0
  N17: LED5.blue_cathode, R6.Pin_0
  N18: LED5.green_cathode, R5.Pin_0
