# Fritzing sketch Lab5 (saved by Fritzing 1.0.1rc)
breadboards: 1

parts:
  U1 = 74HC595 [package="DIP16 [THT]"]
  LED3 = LED - 3mm [color="Yellow (595nm)" current=0.030A package="3 mm [THT]"]
  LED4 = LED - 3mm [color="Yellow (595nm)" current=0.030A package="3 mm [THT]"]
  LED5 = LED - 3mm [color="Red (633nm)" current=0.030A package="3 mm [THT]"]
  LED6 = LED - 3mm [color="Red (633nm)" current=0.030A package="3 mm [THT]"]
  LED7 = LED - 3mm [color="Blue (430nm)" current=0.030A package="3 mm [THT]"]
  LED8 = LED - 3mm [color="Blue (430nm)" current=0.030A package="3 mm [THT]"]
  LED9 = LED - 3mm [color="Green (555nm)" current=0.030A package="3 mm [THT]"]
  LED10 = LED - 3mm [color="Green (555nm)" current=0.030A package="3 mm [THT]"]
  S1 = Pushbutton [package="[THT]"]
  S2 = Pushbutton [package="[THT]"]
  LED11 = 7-SEGMENT-4DIGIT-YOUNGSUN [package=7-segment-4digit-youngsun]
  7_Segment1 = 7 Segment Display
  R1 = Resistor [tolerance=±5% resistance=220 package="1206 [SMD]"]
  R2 = Resistor [tolerance=±5% resistance=220 package="1206 [SMD]"]
  R3 = Resistor [tolerance=±5% resistance=220 package="1206 [SMD]"]
  R4 = Resistor [tolerance=±5% resistance=220 package="1206 [SMD]"]
  R5 = Resistor [tolerance=±5% resistance=220 package="1206 [SMD]"]
  R6 = Resistor [tolerance=±5% resistance=220 package="1206 [SMD]"]
  R7 = Resistor [tolerance=±5% resistance=220 package="1206 [SMD]"]
  R8 = Resistor [tolerance=±5% resistance=220 package="1206 [SMD]"]
  R9 = Resistor [tolerance=±5% resistance=220 package="1206 [SMD]"]
  R10 = Resistor [tolerance=±5% resistance=220 package="1206 [SMD]"]
  R11 = Resistor [tolerance=±5% resistance=220 package="1206 [SMD]"]
  R12 = Resistor [tolerance=±5% resistance=220 package="1206 [SMD]"]
  R13 = Resistor [tolerance=±5% resistance=220 package="1206 [SMD]"]
  R14 = Resistor [tolerance=±5% resistance=220 package="1206 [SMD]"]
  R15 = Resistor [tolerance=±5% resistance=220 package="1206 [SMD]"]
  Part1 = Arduino Mega 2560 (Rev3)

nets:
  N1: U1.Q1, R2.Pin_1, R13.Pin_0, Part1.D22
  N2: U1.Q2, R3.Pin_1, R9.Pin_0, Part1.D24
  N3: U1.Q3, R4.Pin_1, R10.Pin_0, Part1.D25
  N4: U1.Q4, R5.Pin_1, R11.Pin_0, Part1.D26
  N5: U1.Q5, R6.Pin_1, R14.Pin_0, Part1.D27
  N6: U1.Q6, R7.Pin_1, R15.Pin_0, Part1.D28
  N7: U1.Q7, R8.Pin_1
  GND: U1.GND, U1.OE, LED3.cathode, LED4.cathode, LED5.cathode, LED6.cathode, LED7.cathode, LED8.cathode, LED9.cathode, LED10.cathode, S1.Pin_1, S1.Pin_2, S2.Pin_1, S2.Pin_2, 7_Segment1.common_anode, Part1.GND
  VCC: U1.MR, U1.VCC, Part1.5V
  N8: U1.SH_CP, Part1.D19/RX1
  N9: U1.ST_CP, Part1.D20/SDA
  N10: U1.DS, Part1.D21/SCL
  N11: U1.Q0, R1.Pin_1, R12.Pin_0, Part1.D23
  N12: LED3.anode, R1.Pin_0
  N13: LED4.anode, R2.Pin_0
  N14: LED5.anode, R3.Pin_0
  N15: LED6.anode, R4.Pin_0
  N16: LED7.anode, R5.Pin_0
  N17: LED8.anode, R6.Pin_0
  N18: LED9.anode, R7.Pin_0
  N19: LED10.anode, R8.Pin_0
  N20: S1.Pin_3, S1.Pin_4, Part1.D3_PWM
  N21: S2.Pin_3, S2.Pin_4, Part1.D2_PWM
  N22: LED11.DIG1, Part1.D9_PWM
  N23: LED11.DIG2, Part1.D10_PWM
  N24: LED11.E, Part1.D11_PWM
  N25: LED11.DIG3, Part1.D7_PWM
  N26: LED11.DP, Part1.D52
  N27: LED11.APOS-C, Part1.D12_PWM
  N28: LED11.APOS-A, Part1.D4_PWM
  N29: LED11.C, Part1.D5_PWM
  N30: LED11.A, Part1.D8_PWM
  N31: LED11.G, Part1.D13_PWM
  N32: LED11.B, Part1.D6_PWM
  N33: 7_Segment1.Segment_E, R11.Pin_1
  N34: 7_Segment1.Segment_D, R10.Pin_1
  N35: 7_Segment1.Segment_C, R9.Pin_1
  N36: 7_Segment1.Segment_B, R12.Pin_1
  N37: 7_Segment1.Segment_A, R13.Pin_1
  N38: 7_Segment1.Segment_F, R14.Pin_1
  N39: 7_Segment1.Segment_G, R15.Pin_1
