# Fritzing sketch VasuPatelLab6 (saved by Fritzing 1.0.1rc)
breadboards: 1

parts:
  U1 = LCD-16X2 [package=lcd-16x2_noholes]
  S2 = Momentary Switch [package=ksa_sealed_tac_switch]
  LED1 = 7-SEGMENT-4DIGIT-YOUNGSUN [package=7-segment-4digit-youngsun]
  DHT1 = DHT11 Humitidy and Temperature Sensor (3 pins)
  R4 = Rotary Potentiometer (Small) [maximum_resistance=10kΩ knob_status=50% power=0.5W package=THT]
  Part1 = Arduino Mega 2560 (Rev3)
  R5 = Temperature Sensor (Thermistor) [thermistor_type=NTC package=THT]
  R6 = Resistor [tolerance=±5% resistance=220 package="0603 [SMD]"]
  R7 = Resistor [tolerance=±5% resistance=220 package="0603 [SMD]"]

nets:
  VSS: U1.VSS, U1.K, S2.2, DHT1.Plus, R4.leg1, Part1.GND, R6.Pin_0
  VDD: U1.VDD, U1.R_W, DHT1.Signal, R4.leg2, Part1.5V, R5.pin_0, R7.Pin_0
  N1: U1.VO, R4.wiper
  N2: U1.RS, Part1.D21/SCL
  N3: U1.E, Part1.D20/SDA
  N4: U1.DB4, Part1.D19/RX1
  N5: U1.DB5, Part1.D18/TX1
  N6: U1.DB6, Part1.D17_PWM/RX2
  N7: U1.DB7, Part1.D16_PWM/TX2
  N8: U1.A, R7.Pin_1
  N9: S2.4, Part1.D2_PWM
  N10: LED1.DIG2, Part1.D9_PWM
  N11: LED1.D, Part1.D10_PWM
  N12: LED1.COL-A, Part1.D22
  N13: LED1.E, Part1.D11_PWM
  N14: LED1.DIG3, Part1.D7_PWM
  N15: LED1.DP, Part1.D3_PWM
  N16: LED1.APOS-A, Part1.D12_PWM
  N17: LED1.F, Part1.D4_PWM
  N18: LED1.COL-C, Part1.D5_PWM
  N19: LED1.C, Part1.D8_PWM
  N20: LED1.A, Part1.D13_PWM
  N21: LED1.G, Part1.D6_PWM
  N22: DHT1.Gnd, Part1.D15/RX3
  N23: R5.pin_1, R6.Pin_1

custom parts:
  DHT11 Humitidy and Temperature Sensor (3 pins): DHT11 Humidity and Temperature Sensor (3 pins).
